// Logisim project CU.circ as structural Verilog: 1 circuit, main circuit main
module main (
  input  AC_VAL,
  input  DR,
  input  AC15,
  input  E,
  input  FGO,
  input  FGI,
  input  R_prime_T0,
  input  R_prime_T1,
  input  R_prime_T2,
  input  D7_prime_IT3,
  input  T0T1_prime_T2_prime,
  input  RT0,
  input  RT1,
  input  RT2,
  input  D0T4,
  input  D0T5,
  input  D1T4,
  input  D1T5,
  input  D2T4,
  input  D2T5,
  input  D3T4,
  input  D4T4,
  input  D5T4,
  input  D5T5,
  input  D6T4,
  input  D6T5,
  input  D6T6,
  input  rB0,
  input  rB1,
  input  rB2,
  input  rB3,
  input  rB4,
  input  rB5,
  input  rB6,
  input  rB7,
  input  rB8,
  input  rB9,
  input  rB10,
  input  rB11,
  input  pB6,
  input  pB7,
  input  pB8,
  input  pB9,
  input  pB10,
  input  pB11,
  output INCAR,
  output LDAR,
  output CLRAR,
  output R_J,
  output R_K,
  output INCPC,
  output LDPC,
  output CLRPC,
  output READ,
  output WRITE,
  output INCDR,
  output LDDR,
  output LDIR,
  output LDTR,
  output LDAC,
  output INCAC,
  output CLRAC,
  output S0,
  output S1,
  output S2,
  output S____0,
  output AND,
  output ADD,
  output DR_2,
  output INPR,
  output COM,
  output SHR,
  output SHL,
  output E_2,
  output SC__0,
  output IEN__0,
  output IEN__1,
  output LD_OUTR,
  output E__E_prime,
  output E__0
);

  wire not_1_out, not_2_out, not_3_out, not_4_out;
  wire [6:0] and_1_out;

  not not_1 (not_1_out, DR);
  or or_1 (SC__0, D0T5, D1T5, D2T5, D3T4, D4T4, D5T5, D6T6, rB0, rB1, rB2, rB3, rB4, rB5, rB6, rB7, rB8, rB9, rB10, rB11, pB6, pB7, pB8, pB9, pB10, pB11);
  and and_1 (and_1_out[0], not_1_out, D6T6);
  not not_2 (not_2_out, E);
  and and_2 (and_1_out[1], not_2_out, rB1);
  not not_3 (not_3_out, AC_VAL);
  and and_3 (and_1_out[2], not_3_out, rB2);
  and and_4 (and_1_out[3], AC15, rB3);
  not not_4 (not_4_out, AC15);
  and and_5 (and_1_out[4], not_4_out, rB4);
  and and_6 (and_1_out[5], FGO, pB8);
  and and_7 (and_1_out[6], FGI, pB9);
  or or_2 (LDAR, R_prime_T0, R_prime_T2, D7_prime_IT3);
  or or_3 (INCPC, R_prime_T1, RT2, and_1_out[0], and_1_out[1], and_1_out[2], and_1_out[3], and_1_out[4], and_1_out[5], and_1_out[6]);
  or or_4 (LDPC, D4T4, D5T5);
  or or_5 (READ, R_prime_T1, D7_prime_IT3, D0T4, D1T4, D2T4, D6T4);
  or or_6 (WRITE, RT1, D3T4, D5T4, D6T6);
  or or_7 (LDDR, D0T4, D1T4, D2T4, D6T4);
  or or_8 (S0, READ, LDPC, R_prime_T2, D2T5, D6T6);
  or or_9 (S1, READ, D5T4, D6T6, RT1, R_prime_T0, RT0, D2T5);
  or or_10 (S2, READ, D3T4, pB10, R_prime_T2, RT1);
  or or_11 (IEN__0, RT2, pB6);
  or or_12 (E_2, rB6, rB7, rB8, rB10, D1T5);
  or or_13 (LDAC, D1T5, D0T5, D2T5, pB11, rB9, rB7, rB6);

  assign ADD = D1T5;
  assign AND = D0T5;
  assign CLRAC = rB11;
  assign CLRAR = RT0;
  assign CLRPC = RT1;
  assign COM = rB9;
  assign DR_2 = D2T5;
  assign E__0 = rB10;
  assign E__E_prime = rB8;
  assign IEN__1 = pB7;
  assign INCAC = rB5;
  assign INCAR = D5T4;
  assign INCDR = D6T5;
  assign INPR = pB11;
  assign LD_OUTR = pB10;
  assign LDIR = R_prime_T1;
  assign LDTR = RT0;
  assign R_J = T0T1_prime_T2_prime;
  assign R_K = RT2;
  assign S____0 = rB0;
  assign SHL = rB6;
  assign SHR = rB7;
endmodule
