// Logisim project INPRR.circ as structural Verilog: 1 circuit, main circuit main
module main (
  input  CLK,
  input  [7:0] INPUT
);

  wire [7:0] bit_extender_1_out;

  Bit_Extender #(.out_width(8)) bit_extender_1 (.in(INPUT), .out(bit_extender_1_out));
  Counter counter_1 (.D(bit_extender_1_out), .clk(CLK));  // open: load, count, Q, carry, clr
endmodule
