// Logisim project Input-Output-Ref.circ as structural Verilog: 1 circuit, main circuit main
module main (
  input  D7IT3,
  input  [11:0] _12bit_data,
  output rB6,
  output pB7,
  output pB8,
  output pB9,
  output pB10,
  output pB11
);

  and and_1 (rB6, D7IT3, _12bit_data[6]);
  and and_2 (pB7, D7IT3, _12bit_data[7]);
  and and_3 (pB8, D7IT3, _12bit_data[8]);
  and and_4 (pB9, D7IT3, _12bit_data[9]);
  and and_5 (pB10, D7IT3, _12bit_data[10]);
  and and_6 (pB11, D7IT3, _12bit_data[11]);
endmodule
