// Logisim project MAIN.circ as structural Verilog: 1 circuit, main circuit main
module main (
  input  FGI,
  input  FGO,
  input  CLR,
  input  in_4,
  input  INC,
  input  CLR_2,
  output out_7,
  output out_8,
  output [2:0] out_9,
  output [15:0] AR,
  output [15:0] PC,
  output [15:0] DR,
  output E,
  output [15:0] AC,
  output [15:0] IR,
  output [15:0] TR
);

  wire and_1_out, and_2_out, and_3_out, clock_1_out, CONTROL_UNIT_e_2, CONTROL_UNIT_ien__0,
       CONTROL_UNIT_ien__1, CONTROL_UNIT_r_j, CONTROL_UNIT_r_k, CONTROL_UNIT_s____0, CONTROL_UNIT_sc__0,
       decoder_1_out0, decoder_1_out1, decoder_1_out2, decoder_1_out3, decoder_1_out4, decoder_1_out5,
       decoder_1_out6, decoder_1_out7, E_FLAG_q, FGI_q, FGO_q, IR_p2, main_4_ac15, main_4_ac_val,
       main_4_dr_val, MEMORY_REFERENCE_p10, MEMORY_REFERENCE_p22, not_1_out, not_2_out, not_3_out, OUTR_p1,
       TIMER_t0, TIMER_t1, TIMER_t2, TIMER_t3, TIMER_t4, TIMER_t5, TIMER_t6, TIMER_t7, TR_p3;
  wire [1:0] CONTROL_UNIT_read, DR_p2;
  wire [2:0] AC_p3, AR_p2, PC_p2;
  wire [5:0] main_2_rb6;
  wire [6:0] CONTROL_UNIT_and;
  wire [7:0] undriven;
  wire [11:0] main_1_rb0;
  wire [15:0] AR_p1, main_3_ac_output, ram_1_data;
  wire [20:0] MEMORY_REFERENCE_p25;

  counter_main TIMER (
    .Clock(and_1_out), .Clear(MEMORY_REFERENCE_p10), .T0(TIMER_t0), .T1(TIMER_t1), .T2(TIMER_t2),
    .T3(TIMER_t3), .T4(TIMER_t4), .T5(TIMER_t5), .T6(TIMER_t6), .T7(TIMER_t7));
  Clock clock_1 (.out(clock_1_out));
  Register_Ref_main main_1 (
    ._12bit_data(IR[11:0]), .D7I_prime_T3(and_3_out), .rB0(main_1_rb0[0]), .rB1(main_1_rb0[1]),
    .rB2(main_1_rb0[2]), .rB3(main_1_rb0[3]), .rB4(main_1_rb0[4]), .rB5(main_1_rb0[5]), .rB6(main_1_rb0[6]),
    .rB7(main_1_rb0[7]), .rB8(main_1_rb0[8]), .rB9(main_1_rb0[9]), .rB10(main_1_rb0[10]),
    .rB11(main_1_rb0[11]));
  and and_1 (and_1_out, clock_1_out, not_1_out);
  not not_1 (not_1_out, MEMORY_REFERENCE_p22);
  Decoder #(.select(3)) decoder_1 (
    .out0(decoder_1_out0), .out1(decoder_1_out1), .out2(decoder_1_out2), .out3(decoder_1_out3),
    .out4(decoder_1_out4), .out5(decoder_1_out5), .out6(decoder_1_out6), .out7(decoder_1_out7),
    .sel(IR[14:12]));  // open: en
  not not_2 (not_2_out, IR[15]);
  and and_2 (and_2_out, decoder_1_out7, IR[15], TIMER_t3);
  and and_3 (and_3_out, decoder_1_out7, not_2_out, TIMER_t3);
  Input_Output_Ref_main main_2 (
    ._12bit_data(IR[11:0]), .D7IT3(and_2_out), .rB6(main_2_rb6[0]), .pB7(main_2_rb6[1]), .pB8(main_2_rb6[2]),
    .pB9(main_2_rb6[3]), .pB10(main_2_rb6[4]), .pB11(main_2_rb6[5]));
  MY_ALU_main main_3 (
    ._0(in_4), .AND(CONTROL_UNIT_and[0]), .ADD(CONTROL_UNIT_and[1]), .DR(CONTROL_UNIT_and[2]),
    .INPR(CONTROL_UNIT_and[3]), .COM(CONTROL_UNIT_and[4]), .SHR(CONTROL_UNIT_and[5]),
    .SHL(CONTROL_UNIT_and[6]), .DR_INPUT(DR), .INPR_2(undriven), .AC_INPUT(AC), .FROM_E(E_FLAG_q), .E_OUT(E),
    .AC_OUTPUT(main_3_ac_output));
  // Memory_Ref_main MEMORY_REFERENCE: pin names not known; wires that end beside it: TIMER_t0, TIMER_t1, TIMER_t2, TIMER_t3, TIMER_t4, TIMER_t5, TIMER_t6, TIMER_t7, decoder_1_out0, MEMORY_REFERENCE_p10, decoder_1_out1, decoder_1_out2, decoder_1_out3, decoder_1_out4, decoder_1_out5, decoder_1_out6, decoder_1_out7, out_7, out_8, FGI, FGO, MEMORY_REFERENCE_p22, E, IR[15], MEMORY_REFERENCE_p25[0], MEMORY_REFERENCE_p25[1], MEMORY_REFERENCE_p25[2], MEMORY_REFERENCE_p25[3], MEMORY_REFERENCE_p25[4], MEMORY_REFERENCE_p25[5], MEMORY_REFERENCE_p25[6], MEMORY_REFERENCE_p25[7], MEMORY_REFERENCE_p25[8], MEMORY_REFERENCE_p25[9], MEMORY_REFERENCE_p25[10], MEMORY_REFERENCE_p25[11], MEMORY_REFERENCE_p25[12], MEMORY_REFERENCE_p25[13], MEMORY_REFERENCE_p25[14], MEMORY_REFERENCE_p25[15], MEMORY_REFERENCE_p25[16], MEMORY_REFERENCE_p25[17], MEMORY_REFERENCE_p25[18], MEMORY_REFERENCE_p25[19], MEMORY_REFERENCE_p25[20]
  // IncReg12_main AR: pin names not known; wires that end beside it: AR_p1[11:0], AR_p2[0], AR_p2[1], AR_p2[2], AR[11:0], and_1_out
  // IncReg12_main PC: pin names not known; wires that end beside it: AR_p1[11:0], PC_p2[0], PC_p2[1], PC_p2[2], PC[11:0], and_1_out
  // IncReg16_main DR: pin names not known; wires that end beside it: AR_p1, DR_p2[0], DR_p2[1], CLR, DR, and_1_out
  // IncReg16_main AC: pin names not known; wires that end beside it: main_3_ac_output, AC_p3[1], AC_p3[0], AC_p3[2], AC, and_1_out
  INPRR_main INPR (.INPUT(undriven), .CLK(and_1_out));
  // IR_main IR: pin names not known; wires that end beside it: AR_p1, IR_p2, and_1_out, IR
  // IncReg16_main TR: pin names not known; wires that end beside it: AR_p1, INC, TR_p3, CLR_2, TR, and_1_out
  // OUTR_main OUTR: pin names not known; wires that end beside it: OUTR_p1, AR_p1, and_1_out
  D_Flip_Flop u_FGO (.clk(and_1_out), .D(FGO), .Q(FGO_q));  // open: Qn, preset, en, reset
  D_Flip_Flop u_FGI (.clk(and_1_out), .D(FGI), .Q(FGI_q));  // open: Qn, preset, en, reset
  RAM #(.addrWidth(12), .dataWidth(16), .bus("separate")) ram_1 (
    .addr(AR[11:0]), .din(AR_p1), .data(ram_1_data), .str(CONTROL_UNIT_read[1]), .clk(and_1_out),
    .ld(CONTROL_UNIT_read[0]));  // open: sel, clr
  val_extract_main main_4 (.DR(DR), .AC(AC), .AC_Val(main_4_ac_val), .DR_Val(main_4_dr_val), .AC15(main_4_ac15));
  CU_main CONTROL_UNIT (
    .R_prime_T0(MEMORY_REFERENCE_p25[0]), .R_prime_T1(MEMORY_REFERENCE_p25[1]),
    .R_prime_T2(MEMORY_REFERENCE_p25[2]), .D7_prime_IT3(MEMORY_REFERENCE_p25[3]),
    .T0T1_prime_T2_prime(MEMORY_REFERENCE_p25[4]), .RT0(MEMORY_REFERENCE_p25[5]),
    .RT1(MEMORY_REFERENCE_p25[6]), .RT2(MEMORY_REFERENCE_p25[7]), .D0T4(MEMORY_REFERENCE_p25[8]),
    .D0T5(MEMORY_REFERENCE_p25[9]), .D1T4(MEMORY_REFERENCE_p25[10]), .D1T5(MEMORY_REFERENCE_p25[11]),
    .D2T4(MEMORY_REFERENCE_p25[12]), .D2T5(MEMORY_REFERENCE_p25[13]), .D3T4(MEMORY_REFERENCE_p25[14]),
    .D4T4(MEMORY_REFERENCE_p25[15]), .D5T4(MEMORY_REFERENCE_p25[16]), .D5T5(MEMORY_REFERENCE_p25[17]),
    .D6T4(MEMORY_REFERENCE_p25[18]), .D6T5(MEMORY_REFERENCE_p25[19]), .D6T6(MEMORY_REFERENCE_p25[20]),
    .rB0(main_1_rb0[0]), .rB1(main_1_rb0[1]), .rB2(main_1_rb0[2]), .rB3(main_1_rb0[3]), .rB4(main_1_rb0[4]),
    .rB5(main_1_rb0[5]), .rB6(main_1_rb0[6]), .rB7(main_1_rb0[7]), .rB8(main_1_rb0[8]), .rB9(main_1_rb0[9]),
    .rB10(main_1_rb0[10]), .rB11(main_1_rb0[11]), .pB6(main_2_rb6[0]), .pB7(main_2_rb6[1]),
    .pB8(main_2_rb6[2]), .pB9(main_2_rb6[3]), .pB10(main_2_rb6[4]), .pB11(main_2_rb6[5]),
    .AC_VAL(main_4_ac_val), .DR(main_4_dr_val), .AC15(main_4_ac15), .E(out_8), .FGO(FGO_q), .FGI(FGI_q),
    .INCAR(AR_p2[0]), .LDAR(AR_p2[1]), .CLRAR(AR_p2[2]), .R_J(CONTROL_UNIT_r_j), .R_K(CONTROL_UNIT_r_k),
    .INCPC(PC_p2[0]), .LDPC(PC_p2[1]), .CLRPC(PC_p2[2]), .READ(CONTROL_UNIT_read[0]),
    .WRITE(CONTROL_UNIT_read[1]), .INCDR(DR_p2[0]), .LDDR(DR_p2[1]), .LDIR(IR_p2), .LDTR(TR_p3),
    .LDAC(AC_p3[0]), .INCAC(AC_p3[1]), .CLRAC(AC_p3[2]), .S0(out_9[0]), .S1(out_9[1]), .S2(out_9[2]),
    .S____0(CONTROL_UNIT_s____0), .AND(CONTROL_UNIT_and[0]), .ADD(CONTROL_UNIT_and[1]),
    .DR_2(CONTROL_UNIT_and[2]), .INPR(CONTROL_UNIT_and[3]), .COM(CONTROL_UNIT_and[4]),
    .SHR(CONTROL_UNIT_and[5]), .SHL(CONTROL_UNIT_and[6]), .E_2(CONTROL_UNIT_e_2), .SC__0(CONTROL_UNIT_sc__0),
    .IEN__0(CONTROL_UNIT_ien__0), .IEN__1(CONTROL_UNIT_ien__1), .LD_OUTR(OUTR_p1));  // open: E__E_prime, E__0
  Multiplexer #(.select(3), .width(16)) multiplexer_1 (
    .in1(AR), .in2(PC), .in3(DR), .in4(AC), .in5(IR), .in6(TR), .in7(ram_1_data), .out(AR_p1), .sel(out_9));  // open: in0, en
  J_K_Flip_Flop R_FLAG (
    .J(CONTROL_UNIT_r_j), .clk(and_1_out), .K(CONTROL_UNIT_r_k), .Q(out_7));  // open: Qn, preset, en, reset
  not not_3 (not_3_out, CONTROL_UNIT_sc__0);
  D_Flip_Flop S_FLAG (
    .clk(and_1_out), .D(CONTROL_UNIT_s____0), .Q(MEMORY_REFERENCE_p22));  // open: Qn, preset, en, reset
  J_K_Flip_Flop SC (
    .J(CONTROL_UNIT_sc__0), .clk(and_1_out), .K(not_3_out), .Q(MEMORY_REFERENCE_p10));  // open: Qn, preset, en, reset
  J_K_Flip_Flop IEN_FLAG (
    .J(CONTROL_UNIT_ien__0), .clk(and_1_out), .K(CONTROL_UNIT_ien__1), .Q(out_8));  // open: Qn, preset, en, reset
  D_Flip_Flop E_FLAG (.clk(and_1_out), .D(E), .Q(E_FLAG_q), .en(CONTROL_UNIT_e_2));  // open: Qn, preset, reset

  // Notes on the sheet:
  //   MEMORY
endmodule
