// Logisim project MY_ALU.circ as structural Verilog: 1 circuit, main circuit main
module main (
  input  _0,
  input  AND,
  input  ADD,
  input  DR,
  input  INPR,
  input  COM,
  input  SHR,
  input  SHL,
  input  FROM_E,
  input  [15:0] DR_INPUT,
  input  [7:0] INPR_2,
  input  [15:0] AC_INPUT,
  output E_OUT,
  output [15:0] AC_OUTPUT
);

  wire A1_p6, A2_p4, A3_p1, A3_p6, A5_p2, A5_p4, A6_p4, A7_p4, A9_p2, A9_p4, A10_p4, A11_p4, A13_p2, A13_p4,
       A14_p4, A15_p4, A16_p4, and_1_out, and_2_out, or_2_out;

  // adder_lc_main A1: pin names not known; wires that end beside it: ADD, INPR, AND, _0, ADD, A1_p6, DR, INPR, COM, SHR, AC_INPUT[1], SHL, FROM_E, INPR_2[0], AC_INPUT[0], AC_OUTPUT[0], DR_INPUT[0]
  // adder_lc_main A5: pin names not known; wires that end beside it: AND, A5_p2, ADD, A5_p4, DR, INPR, COM, SHR, AC_INPUT[5], SHL, AC_INPUT[3], INPR_2[4], AC_INPUT[4], AC_OUTPUT[4], DR_INPUT[4]
  // adder_lc_main A9: pin names not known; wires that end beside it: AND, A9_p2, ADD, A9_p4, DR, INPR, COM, SHR, AC_INPUT[9], SHL, AC_INPUT[7], _0, AC_INPUT[8], AC_OUTPUT[8], DR_INPUT[8]
  // adder_lc_main A13: pin names not known; wires that end beside it: AND, A13_p2, ADD, A13_p4, DR, INPR, COM, SHR, AC_INPUT[13], SHL, AC_INPUT[11], _0, AC_INPUT[12], AC_OUTPUT[12], DR_INPUT[12]
  and and_1 (and_1_out, AC_INPUT[0], SHR);
  // adder_lc_main A2: pin names not known; wires that end beside it: AND, A1_p6, ADD, A2_p4, DR, INPR, COM, SHR, AC_INPUT[2], SHL, AC_INPUT[0], INPR_2[1], AC_INPUT[1], AC_OUTPUT[1], DR_INPUT[1]
  // adder_lc_main A6: pin names not known; wires that end beside it: AND, A5_p4, ADD, A6_p4, DR, INPR, COM, SHR, AC_INPUT[6], SHL, AC_INPUT[4], INPR_2[5], AC_INPUT[5], AC_OUTPUT[5], DR_INPUT[5]
  // adder_lc_main A10: pin names not known; wires that end beside it: AND, A9_p4, ADD, A10_p4, DR, INPR, COM, SHR, AC_INPUT[10], SHL, AC_INPUT[8], AC_INPUT[9], AC_OUTPUT[9], DR_INPUT[9]
  // adder_lc_main A14: pin names not known; wires that end beside it: AND, A13_p4, ADD, A14_p4, DR, INPR, COM, SHR, AC_INPUT[14], SHL, AC_INPUT[12], AC_INPUT[13], AC_OUTPUT[13], DR_INPUT[13]
  // adder_lc_main A3: pin names not known; wires that end beside it: A3_p1, A3_p1, AND, A2_p4, ADD, A3_p6, DR, INPR, COM, SHR, AC_INPUT[3], SHL, AC_INPUT[1], INPR_2[2], AC_INPUT[2], AC_OUTPUT[2], DR_INPUT[2]
  // adder_lc_main A7: pin names not known; wires that end beside it: AND, A6_p4, ADD, A7_p4, DR, INPR, COM, SHR, AC_INPUT[7], SHL, AC_INPUT[5], INPR_2[6], AC_INPUT[6], AC_OUTPUT[6], DR_INPUT[6]
  // adder_lc_main A11: pin names not known; wires that end beside it: AND, A10_p4, ADD, A11_p4, DR, INPR, COM, SHR, AC_INPUT[11], SHL, AC_INPUT[9], AC_INPUT[10], AC_OUTPUT[10], DR_INPUT[10]
  // adder_lc_main A15: pin names not known; wires that end beside it: AND, A14_p4, ADD, A15_p4, DR, INPR, COM, SHR, AC_INPUT[15], SHL, AC_INPUT[13], AC_INPUT[14], AC_OUTPUT[14], DR_INPUT[14]
  // adder_lc_main A4: pin names not known; wires that end beside it: AND, A3_p6, ADD, A5_p2, DR, INPR, COM, SHR, AC_INPUT[4], SHL, AC_INPUT[2], INPR_2[3], AC_INPUT[3], AC_OUTPUT[3], DR_INPUT[3]
  // adder_lc_main A8: pin names not known; wires that end beside it: AND, A7_p4, ADD, A9_p2, DR, INPR, COM, SHR, AC_INPUT[8], SHL, AC_INPUT[6], INPR_2[7], AC_INPUT[7], AC_OUTPUT[7], DR_INPUT[7]
  // adder_lc_main A12: pin names not known; wires that end beside it: AND, A11_p4, ADD, A13_p2, DR, INPR, COM, SHR, AC_INPUT[12], SHL, AC_INPUT[10], AC_INPUT[11], AC_OUTPUT[11], DR_INPUT[11]
  // adder_lc_main A16: pin names not known; wires that end beside it: AND, A15_p4, ADD, A16_p4, DR, INPR, COM, SHR, FROM_E, SHL, AC_INPUT[14], AC_INPUT[15], AC_OUTPUT[15], DR_INPUT[15]
  and and_2 (and_2_out, AC_INPUT[15], SHL);
  or or_1 (E_OUT, A16_p4, or_2_out);
  or or_2 (or_2_out, and_1_out, and_2_out);

  // Other names for the same wires on the sheet: AC0 = AC_INPUT[0]; AC1 = AC_INPUT[1]; AC2 = AC_INPUT[2];
  //   AC3 = AC_INPUT[3]; AC4 = AC_INPUT[4]; AC5 = AC_INPUT[5]; AC6 = AC_INPUT[6]; AC7 = AC_INPUT[7];
  //   AC8 = AC_INPUT[8]; AC9 = AC_INPUT[9]; AC10 = AC_INPUT[10]; AC11 = AC_INPUT[11]; AC12 = AC_INPUT[12];
  //   AC13 = AC_INPUT[13]; AC14 = AC_INPUT[14]; AC15 = AC_INPUT[15]; A_prime_0 = AC_OUTPUT[0];
  //   A_prime_1 = AC_OUTPUT[1]; A_prime_2 = AC_OUTPUT[2]; A_prime_3 = AC_OUTPUT[3]; A_prime_4 = AC_OUTPUT[4];
  //   A_prime_5 = AC_OUTPUT[5]; A_prime_6 = AC_OUTPUT[6]; A_prime_7 = AC_OUTPUT[7]; A_prime_8 = AC_OUTPUT[8];
  //   A_prime_9 = AC_OUTPUT[9]; A_prime_10 = AC_OUTPUT[10]; A_prime_11 = AC_OUTPUT[11]; A_prime_12 = AC_OUTPUT[12];
  //   A_prime_13 = AC_OUTPUT[13]; A_prime_14 = AC_OUTPUT[14]; A_prime_15 = AC_OUTPUT[15]; DR0 = DR_INPUT[0];
  //   DR1 = DR_INPUT[1]; DR2 = DR_INPUT[2]; DR3 = DR_INPUT[3]; DR4 = DR_INPUT[4]; DR5 = DR_INPUT[5];
  //   DR6 = DR_INPUT[6]; DR7 = DR_INPUT[7]; DR8 = DR_INPUT[8]; DR9 = DR_INPUT[9]; DR10 = DR_INPUT[10];
  //   DR11 = DR_INPUT[11]; DR12 = DR_INPUT[12]; DR13 = DR_INPUT[13]; DR14 = DR_INPUT[14]; DR15 = DR_INPUT[15];
  //   I1 = INPR_2[0]; I2 = INPR_2[1]; I3 = INPR_2[2]; I4 = INPR_2[3]; I5 = INPR_2[4]; I6 = INPR_2[5]; I7 = INPR_2[6];
  //   I8 = INPR_2[7]
endmodule
