// Logisim project Register-Ref.circ as structural Verilog: 1 circuit, main circuit main
module main (
  input  D7I_prime_T3,
  input  [11:0] _12bit_data,
  output rB0,
  output rB1,
  output rB2,
  output rB3,
  output rB4,
  output rB5,
  output rB6,
  output rB7,
  output rB8,
  output rB9,
  output rB10,
  output rB11
);

  and and_1 (rB0, D7I_prime_T3, _12bit_data[0]);
  and and_2 (rB1, D7I_prime_T3, _12bit_data[1]);
  and and_3 (rB2, D7I_prime_T3, _12bit_data[2]);
  and and_4 (rB3, D7I_prime_T3, _12bit_data[3]);
  and and_5 (rB4, D7I_prime_T3, _12bit_data[4]);
  and and_6 (rB5, D7I_prime_T3, _12bit_data[5]);
  and and_7 (rB6, D7I_prime_T3, _12bit_data[6]);
  and and_8 (rB7, D7I_prime_T3, _12bit_data[7]);
  and and_9 (rB8, D7I_prime_T3, _12bit_data[8]);
  and and_10 (rB9, D7I_prime_T3, _12bit_data[9]);
  and and_11 (rB10, D7I_prime_T3, _12bit_data[10]);
  and and_12 (rB11, D7I_prime_T3, _12bit_data[11]);
endmodule
